# Fritzing sketch 200220PhotoSequencer_leds (saved by Fritzing 0.9.3b)
circuit board: 50cm x 4cm
breadboards: 1

parts:
  R2 = Resistor [tolerance=±5% resistance=220 package=THT]
  R3 = Resistor [tolerance=±5% resistance=220 package=THT]
  R4 = Resistor [tolerance=±5% resistance=220 package=THT]
  R5 = Resistor [tolerance=±5% resistance=220 package=THT]
  R6 = Resistor [tolerance=±5% resistance=220 package=THT]
  R7 = Resistor [tolerance=±5% resistance=220 package=THT]
  R8 = Resistor [tolerance=±5% resistance=220 package=THT]
  R9 = Resistor [tolerance=±5% resistance=220 package=THT]
  R10 = Resistor [tolerance=±5% resistance=220 package=THT]
  R11 = Resistor [tolerance=±5% resistance=220 package=THT]
  R12 = Resistor [tolerance=±5% resistance=220 package=THT]
  R13 = Resistor [tolerance=±5% resistance=220 package=THT]
  R14 = Resistor [tolerance=±5% resistance=220 package=THT]
  R15 = Resistor [tolerance=±5% resistance=220 package=THT]
  R16 = Resistor [tolerance=±5% resistance=220 package=THT]
  R17 = Resistor [tolerance=±5% resistance=220 package=THT]
  U2 = 74HC165 [part_number=SN74LS165 package="DIP16 [THT]"]
  U1 = 74HC165 [part_number=SN74LS165 package="DIP16 [THT]"]
  R18 = Resistor [tolerance=±5% resistance=220 package=THT]
  J2 = female pin header, 5 pins [form="♀ (female)"]
  R19 = Resistor [tolerance=±5% resistance=220 package=THT]
  R20 = Resistor [tolerance=±5% resistance=220 package=THT]
  R21 = Resistor [tolerance=±5% resistance=220 package=THT]
  R22 = Resistor [tolerance=±5% resistance=220 package=THT]
  R23 = Resistor [tolerance=±5% resistance=220 package=THT]
  R24 = Resistor [tolerance=±5% resistance=220 package=THT]
  R25 = Resistor [tolerance=±5% resistance=220 package=THT]
  R26 = Resistor [tolerance=±5% resistance=220 package=THT]
  R27 = Resistor [tolerance=±5% resistance=220 package=THT]
  R28 = Resistor [tolerance=±5% resistance=220 package=THT]
  R29 = Resistor [tolerance=±5% resistance=220 package=THT]
  R30 = Resistor [tolerance=±5% resistance=220 package=THT]
  R31 = Resistor [tolerance=±5% resistance=220 package=THT]
  R32 = Resistor [tolerance=±5% resistance=220 package=THT]
  R33 = Resistor [tolerance=±5% resistance=220 package=THT]

nets:
  GND: R2.Pin_0, R3.Pin_0, R4.Pin_0, R5.Pin_0, R6.Pin_0, R7.Pin_0, R8.Pin_0, R9.Pin_0, R10.Pin_0, R11.Pin_0, R12.Pin_0, R13.Pin_0, R14.Pin_0, R15.Pin_0, R16.Pin_0, R17.Pin_0, U2.GND, U2.OE, U1.GND, U1.OE, J2.pin4
  N1: R2.Pin_1, R18.Pin_1
  N2: R3.Pin_1, R21.Pin_0
  N3: R4.Pin_1, R19.Pin_0
  N4: R5.Pin_1, R20.Pin_0
  N5: R6.Pin_1, R23.Pin_0
  N6: R7.Pin_1, R22.Pin_0
  N7: R8.Pin_1, R25.Pin_0
  N8: R9.Pin_1, R24.Pin_0
  N9: R10.Pin_1, R33.Pin_0
  N10: R11.Pin_1, R32.Pin_0
  N11: R12.Pin_1, R28.Pin_0
  N12: R13.Pin_1, R27.Pin_0
  N13: R14.Pin_1, R26.Pin_1
  N14: R15.Pin_1, R30.Pin_0
  N15: R16.Pin_1, R29.Pin_0
  N16: R17.Pin_1, R31.Pin_0
  N17: U2.Q1, R21.Pin_1
  N18: U2.Q2, R19.Pin_1
  N19: U2.Q3, R20.Pin_1
  N20: U2.Q4, R22.Pin_1
  N21: U2.Q5, R23.Pin_1
  N22: U2.Q6, R24.Pin_1
  N23: U2.Q7, R25.Pin_1
  N24: U2.Q7', U1.DS
  VCC: U2.MR, U2.VCC, U1.MR, U1.VCC, J2.pin5
  N25: U2.SH_CP, U1.SH_CP, J2.pin1
  N26: U2.ST_CP, U1.ST_CP, J2.pin2
  N27: U2.DS, J2.pin3
  N28: U2.Q0, R18.Pin_0
  N29: U1.Q1, R27.Pin_1
  N30: U1.Q2, R28.Pin_1
  N31: U1.Q3, R29.Pin_1
  N32: U1.Q4, R30.Pin_1
  N33: U1.Q5, R31.Pin_1
  N34: U1.Q6, R32.Pin_1
  N35: U1.Q7, R33.Pin_1
  N36: U1.Q0, R26.Pin_0

notes:
  5V GND1 D11 D10 D13
  in
  imui sled

custom parts:
  74HC165: 8-bit parallel-load shift registers
