# Fritzing sketch 200312PhotoSequencer_lngs_Jst_connector (saved by Fritzing 0.9.3b)
circuit board: 50cm x 4cm
breadboards: 1

parts:
  R2 = Resistor [tolerance=±5% resistance=220 package=THT]
  R3 = Resistor [tolerance=±5% resistance=220 package=THT]
  R4 = Resistor [tolerance=±5% resistance=220 package=THT]
  R5 = Resistor [tolerance=±5% resistance=220 package=THT]
  R6 = Resistor [tolerance=±5% resistance=220 package=THT]
  R7 = Resistor [tolerance=±5% resistance=220 package=THT]
  R8 = Resistor [tolerance=±5% resistance=220 package=THT]
  R9 = Resistor [tolerance=±5% resistance=220 package=THT]
  R10 = Resistor [tolerance=±5% resistance=220 package=THT]
  R11 = Resistor [tolerance=±5% resistance=220 package=THT]
  R12 = Resistor [tolerance=±5% resistance=220 package=THT]
  R13 = Resistor [tolerance=±5% resistance=220 package=THT]
  R14 = Resistor [tolerance=±5% resistance=220 package=THT]
  R15 = Resistor [tolerance=±5% resistance=220 package=THT]
  R16 = Resistor [tolerance=±5% resistance=220 package=THT]
  R17 = Resistor [tolerance=±5% resistance=220 package=THT]
  U2 = 74HC165 [part_number=SN74LS165 package="DIP16 [THT]"]
  U1 = 74HC165 [part_number=SN74LS165 package="DIP16 [THT]"]
  R18 = Resistor [tolerance=±5% resistance=220 package=THT]
  R19 = Resistor [tolerance=±5% resistance=220 package=THT]
  R20 = Resistor [tolerance=±5% resistance=220 package=THT]
  R21 = Resistor [tolerance=±5% resistance=220 package=THT]
  R22 = Resistor [tolerance=±5% resistance=220 package=THT]
  R23 = Resistor [tolerance=±5% resistance=220 package=THT]
  R24 = Resistor [tolerance=±5% resistance=220 package=THT]
  R25 = Resistor [tolerance=±5% resistance=220 package=THT]
  R26 = Resistor [tolerance=±5% resistance=220 package=THT]
  R27 = Resistor [tolerance=±5% resistance=220 package=THT]
  R28 = Resistor [tolerance=±5% resistance=220 package=THT]
  R29 = Resistor [tolerance=±5% resistance=220 package=THT]
  R30 = Resistor [tolerance=±5% resistance=220 package=THT]
  R31 = Resistor [tolerance=±5% resistance=220 package=THT]
  R32 = Resistor [tolerance=±5% resistance=220 package=THT]
  R33 = Resistor [tolerance=±5% resistance=220 package=THT]
  J2 = molex pin header, 6 pins [form=molex]
  J1 = molex pin header, 6 pins [form=molex]

nets:
  N1: R2.Pin_0, R3.Pin_0, R4.Pin_0, R5.Pin_0, R6.Pin_0, R7.Pin_0, R8.Pin_0, R9.Pin_0, R10.Pin_0, R11.Pin_0, R12.Pin_0, R13.Pin_0, R14.Pin_0, R15.Pin_0, R16.Pin_0, R17.Pin_0, J2.pin6, J1.pin6
  N2: R2.Pin_1, R33.Pin_0
  N3: R3.Pin_1, R31.Pin_0
  N4: R4.Pin_1, R32.Pin_0
  N5: R5.Pin_1, R30.Pin_0
  N6: R6.Pin_1, R27.Pin_1
  N7: R7.Pin_1, R26.Pin_1
  N8: R8.Pin_1, R29.Pin_1
  N9: R9.Pin_1, R28.Pin_1
  N10: R10.Pin_1, R21.Pin_1
  N11: R11.Pin_1, R20.Pin_1
  N12: R12.Pin_1, R23.Pin_0
  N13: R13.Pin_1, R24.Pin_0
  N14: R14.Pin_1, R25.Pin_0
  N15: R15.Pin_1, R18.Pin_1
  N16: R16.Pin_1, R22.Pin_0
  N17: R17.Pin_1, R19.Pin_1
  N18: U2.Q1, U1.Q1, J2.pin3, J1.pin3
  N19: U2.Q2, U1.Q2, J2.pin1, J1.pin1
  GND: U2.GND, U1.GND, U1.Q0, J2.pin5, J1.pin5
  N20: U2.Q7', J2.pin2
  N21: R18.Pin_0, R19.Pin_0, R20.Pin_0, R21.Pin_0, R22.Pin_1, R23.Pin_1, R24.Pin_1, R25.Pin_1, R26.Pin_0, R27.Pin_0, R28.Pin_0, R29.Pin_0, R30.Pin_1, R31.Pin_1, R32.Pin_1, R33.Pin_1, J2.pin4, J1.pin4

notes:
  5V GND1 GND2 D9 NeXt D13
  5V GND1 GND2 D9 D12 D13
  in
  out
  imui sQ1.3

custom parts:
  74HC165: 8-bit parallel-load shift registers
