# Fritzing sketch SQ13_Arduino (saved by Fritzing 0.9.3b)
circuit board: 1.9cm x 5.5436cm
breadboards: 1

parts:
  Part1 = Arduino Nano (Rev3.0)
  J1 = molex pin header, 6 pins [form=molex]
  J2 = molex pin header, 5 pins [form=molex]

nets:
  N1: Part1.GND, J1.pin4, J1.pin5, J2.pin4
  N2: Part1.D9, J1.pin3
  N3: Part1.D10, J2.pin2
  N4: Part1.D11/MOSI, J2.pin3
  N5: Part1.D12/MISO, J1.pin2
  N6: Part1.5V, J1.pin6, J2.pin5
  N7: Part1.D13/SCK, J1.pin1, J2.pin1

notes:
  USB
  5v
  + gnd 11 10 13
  gnd1_2
  9 12 13
  imui sq1.3 ctrl
  info@imui.org
